// Logisim project dado_dig.circ as structural Verilog: 1 circuit, main circuit main
module main (
  output out_1,
  output out_2,
  output out_3,
  output out_4,
  output out_5,
  output out_6,
  output out_7
);

  wire and_1_out, clock_1_out, j_k_ff_1_q, j_k_ff_1_qn, j_k_ff_2_q, j_k_ff_2_qn, j_k_ff_3_q, j_k_ff_3_qn,
       nand_1_out, nand_2_out, not_1_out;

  Clock clock_1 (.out(clock_1_out));
  J_K_Flip_Flop #(.trigger("falling")) j_k_ff_1 (
    .J(1'b1), .clk(clock_1_out), .K(1'b1), .Q(j_k_ff_1_q), .Qn(j_k_ff_1_qn), .preset(and_1_out));  // open: en, reset
  J_K_Flip_Flop #(.trigger("falling")) j_k_ff_2 (
    .J(1'b1), .clk(j_k_ff_1_q), .K(1'b1), .Q(j_k_ff_2_q), .Qn(j_k_ff_2_qn), .reset(and_1_out));  // open: preset, en
  J_K_Flip_Flop #(.trigger("falling")) j_k_ff_3 (
    .J(1'b1), .clk(j_k_ff_2_q), .K(1'b1), .Q(j_k_ff_3_q), .Qn(j_k_ff_3_qn), .reset(and_1_out));  // open: preset, en
  and and_1 (and_1_out, j_k_ff_3_q, j_k_ff_2_q, j_k_ff_1_q);
  nand nand_1 (nand_1_out, j_k_ff_2_qn, j_k_ff_3_qn, 1'b1);
  nand nand_2 (nand_2_out, j_k_ff_3_q, 1'b1, j_k_ff_2_q);
  not not_1 (not_1_out, nand_1_out);
  not not_2 (out_1, not_1_out);
  not not_3 (out_3, nand_2_out);
  not not_4 (out_4, j_k_ff_1_qn);
  not not_5 (out_6, j_k_ff_3_qn);
  not not_6 (out_2, j_k_ff_3_qn);
  not not_7 (out_5, nand_2_out);
  not not_8 (out_7, not_1_out);
endmodule
